# Fritzing sketch luci (saved by Fritzing 1.0.5)
breadboards: 1

parts:
  LED1 = LED - 5mm [color="Red (633nm)" current=0.030A package="5 mm [THT]"]
  LED2 = LED - 5mm [color="Red (633nm)" current=0.030A package="5 mm [THT]"]
  R2 = Resistor [tolerance=±2% resistance=220 package="1206 [SMD]"]
  R3 = Resistor [tolerance=±2% resistance=220 package="1206 [SMD]"]
  Mod1 = Raspberry Pi 4B
  LED3 = LED - 5mm [color="White (4500K)" current=0.030A package="5 mm [THT]"]
  LED4 = LED - 5mm [color="White (4500K)" current=0.030A package="5 mm [THT]"]
  R4 = Resistor [tolerance=±2% resistance=220 package="1206 [SMD]"]
  R5 = Resistor [tolerance=±2% resistance=220 package="1206 [SMD]"]
  LED5 = LED - 5mm [color="Yellow (595nm)" current=0.030A package="5 mm [THT]"]
  LED6 = LED - 5mm [color="Yellow (595nm)" current=0.030A package="5 mm [THT]"]
  LED7 = LED - 5mm [color="Yellow (595nm)" current=0.030A package="5 mm [THT]"]
  LED8 = LED - 5mm [color="Yellow (595nm)" current=0.030A package="5 mm [THT]"]
  R6 = Resistor [tolerance=±2% resistance=220 package="1206 [SMD]"]
  R7 = Resistor [tolerance=±2% resistance=220 package="1206 [SMD]"]
  R8 = Resistor [tolerance=±2% resistance=220 package="1206 [SMD]"]
  R9 = Resistor [tolerance=±2% resistance=220 package="1206 [SMD]"]
  LED9 = LED - 5mm [color="White (4500K)" current=0.030A package="5 mm [THT]"]
  LED10 = LED - 5mm [color="White (4500K)" current=0.030A package="5 mm [THT]"]
  LED11 = RGB LED (com. cathode, rgb) [color="Red (633nm)" current=0.030A package="5 mm [THT]"]
  LED12 = RGB LED (com. cathode, rgb) [color="Red (633nm)" current=0.030A package="5 mm [THT]"]
  R10 = Resistor [tolerance=±2% resistance=220 package="1206 [SMD]"]
  R11 = Resistor [tolerance=±2% resistance=220 package="1206 [SMD]"]
  R12 = Resistor [tolerance=±1% power=0.25W resistance=220 package=THT]
  R13 = Resistor [tolerance=±2% resistance=220 package="1206 [SMD]"]
  R14 = Resistor [tolerance=±2% resistance=220 package="1206 [SMD]"]

nets:
  N1: LED1.cathode, R3.Pin_0
  N2: LED1.anode, LED2.anode, Mod1.GPIO13
  N3: LED2.cathode, R2.Pin_0
  N4: R2.Pin_1, R3.Pin_1, Mod1.GND, R4.Pin_0, R5.Pin_0, R6.Pin_0, R7.Pin_0, R8.Pin_1, R9.Pin_1, LED11.common_cathode, LED12.common_cathode, R10.Pin_1, R11.Pin_1
  N5: Mod1.GPIO27, LED9.anode, LED10.anode
  N6: Mod1.GPIO22, LED7.anode, LED8.anode
  N7: Mod1.GPIO10, R13.Pin_1
  N8: Mod1.GPIO9, R12.Pin_1
  N9: Mod1.GPIO25, R14.Pin_1
  N10: Mod1.GPIO5, LED5.anode, LED6.anode
  N11: Mod1.GPIO6, LED3.anode, LED4.anode
  N12: LED3.cathode, R5.Pin_1
  N13: LED4.cathode, R4.Pin_1
  N14: LED5.cathode, R7.Pin_1
  N15: LED6.cathode, R6.Pin_1
  N16: LED7.cathode, R8.Pin_0
  N17: LED8.cathode, R9.Pin_0
  N18: LED9.cathode, R10.Pin_0
  N19: LED10.cathode, R11.Pin_0
  N20: LED11.red_anode, LED12.red_anode, R12.Pin_0
  N21: LED11.green_anode, LED12.green_anode, R14.Pin_0
  N22: LED11.blue_anode, LED12.blue_anode, R13.Pin_0
