# Fritzing sketch motori_batterie (saved by Fritzing 1.0.5)
breadboards: 1

parts:
  Mod1 = Raspberry Pi 4B
  S1 = H-Bridge with L298N
  S2 = H-Bridge with L298N
  BATT2 = 4xAA Switchable Battery Pack w/Bare Wire
  M1 = DC Motor [voltage_(max)=6V voltage_(min)=3V]
  M2 = DC Motor [voltage_(max)=6V voltage_(min)=3V]
  M3 = DC Motor [voltage_(max)=6V voltage_(min)=3V]
  M4 = DC Motor [voltage_(max)=6V voltage_(min)=3V]
  BATT3 = 4xAA Switchable Battery Pack w/Bare Wire

nets:
  N1: Mod1.GPIO2, S2.IN1
  N2: Mod1.GPIO3, S2.IN2
  GND: Mod1.GND, S1.GND, S2.GND, BATT2.NEG, BATT3.NEG
  N3: Mod1.GPIO4, S2.IN3
  N4: Mod1.GPIO14, S2.IN4
  N5: Mod1.GPIO15, S2.ENA
  N6: Mod1.GPIO18, S2.ENB
  N7: Mod1.GPIO12, S1.ENA
  N8: Mod1.GPIO19, S1.ENB
  N9: Mod1.GPIO16, S1.IN1
  N10: Mod1.GPIO26, S1.IN4
  N11: Mod1.GPIO20, S1.IN2
  N12: Mod1.GPIO21, S1.IN3
  N13: S1.12V, BATT3.POS
  N14: S1.M1-01, M4.pin_2
  N15: S1.M1-02, M4.pin_1
  N16: S1.M2-01, M3.pin_1
  N17: S1.M2-02, M3.pin_2
  N18: S2.12V, BATT2.POS
  N19: S2.M1-01, M2.pin_1
  N20: S2.M1-02, M2.pin_2
  N21: S2.M2-01, M1.pin_2
  N22: S2.M2-02, M1.pin_1

custom parts:
  H-Bridge with L298N: h-bridge
  4xAA Switchable Battery Pack w/Bare Wire: 4xAA Switchable Battery Pack with Bare Wire connection
